// Logisim project 2018214184-李嘉文-实验一 寄存器实验.circ as structural Verilog: 7 circuits, main circuit main
module main (
  input  [7:0] in_1,
  input  AEN,
  input  WEN,
  input  SA,
  input  SB
);

  wire clock_1_out, R0, R1, R2, R3;
  wire [7:0] controlled_buffer_1_out, register_2_q, register_4_q, \右移电路_1_out_2 , \左移电路_1_out_2 ,
       \直传电路_1_out_2 ;

  Clock #(.highDuration(1), .lowDuration(1)) clock_1 (.out(clock_1_out));
  \左移电路  \u_左移电路_1  (.out_2(\左移电路_1_out_2 ), .in_1(controlled_buffer_1_out));
  Register #(.width(8), .trigger("falling"), .Select("low")) register_1 (
    .D(\左移电路_1_out_2 ), .clk(clock_1_out));  // open: en, Q, clr
  \直传电路  \u_直传电路_1  (.out_2(\直传电路_1_out_2 ), .in_1(controlled_buffer_1_out));
  Register #(.width(8), .trigger("rising"), .Select("low")) register_2 (
    .D(in_1), .en(AEN), .Q(register_2_q), .clk(clock_1_out));  // open: clr
  assign controlled_buffer_1_out = AEN ? register_2_q : 8'bz;  // Controlled_Buffer controlled_buffer_1
  Register #(.width(8), .trigger("falling"), .Select("low")) register_3 (
    .D(\直传电路_1_out_2 ), .clk(clock_1_out));  // open: en, Q, clr
  \右移电路  \u_右移电路_1  (.out_2(\右移电路_1_out_2 ), .in_1(controlled_buffer_1_out));
  Register #(.width(8), .trigger("rising"), .Select("low")) register_4 (
    .D(in_1), .en(WEN), .Q(register_4_q), .clk(clock_1_out));  // open: clr
  Register #(.width(8), .trigger("falling"), .Select("low")) register_5 (
    .D(\右移电路_1_out_2 ), .clk(clock_1_out));  // open: en, Q, clr
  assign controlled_buffer_1_out = WEN ? register_4_q : 8'bz;  // Controlled_Buffer controlled_buffer_2
  \选择电路  \u_选择电路_1  (.in_1(SA), .in_2(SB), .out_3(R0), .out_4(R1), .out_5(R2), .out_6(R3));
  Register #(.width(8), .trigger("rising"), .Select("low")) u_R0 (
    .D(in_1), .en(R0), .clk(clock_1_out));  // open: Q, clr
  Register #(.width(8), .trigger("rising"), .Select("low")) u_R1 (
    .D(in_1), .en(R1), .clk(clock_1_out));  // open: Q, clr
  Register #(.width(8), .trigger("rising"), .Select("low")) u_R2 (
    .D(in_1), .en(R2), .clk(clock_1_out));  // open: Q, clr
  Register #(.width(8), .trigger("rising"), .Select("low")) u_R3 (
    .D(in_1), .en(R3), .clk(clock_1_out));  // open: Q, clr

  // Notes on the sheet:
  //   L
  //   A
  //   D
  //   R
  //   W
endmodule

module \直传电路  (
  input  [7:0] in_1,
  output [7:0] out_2
);


  assign out_2 = in_1;
endmodule

module \左移电路  (
  input  [7:0] in_1,
  output [7:0] out_2
);


  assign out_2 = {in_1[6:0], 1'b0};
endmodule

module \右移电路  (
  input  [7:0] in_1,
  output [7:0] out_2
);


  assign out_2 = {1'b0, in_1[7:1]};
endmodule

module \选择电路  (
  input  in_1,
  input  in_2,
  output out_3,
  output out_4,
  output out_5,
  output out_6
);

  Decoder #(.select(2), .tristate("false"), .disabled("Z"), .enable("false")) decoder_1 (
    .out0(out_3), .out1(out_4), .out2(out_5), .out3(out_6), .sel({in_1, in_2}));
endmodule

module \寄存器使用示例  (
  input  [7:0] in_1,
  input  in_2,
  input  in_3
);

  wire clock_1_out;
  wire [7:0] register_1_q;

  Register #(.width(8), .trigger("falling"), .Select("low")) register_1 (
    .D(in_1), .en(in_2), .Q(register_1_q), .clk(clock_1_out), .clr(in_3));
  Clock #(.highDuration(1), .lowDuration(1)) clock_1 (.out(clock_1_out));
  Hex_Digit_Display hex_digit_display_1 (.value(register_1_q[7:4]));  // open: dp
  Hex_Digit_Display hex_digit_display_2 (.value(register_1_q[3:0]));  // open: dp

  // Notes on the sheet:
  //   高端
  //   Enable(使能端)
  //   时钟触发方式
  //   四种触发方式
  //   清0端
endmodule

module \总线连接模式示例  (
  input  [7:0] \公用输入端 ,
  input  Reset,
  input  AEN,
  input  WEN
);

  wire clock_1_out;
  wire [3:0] controlled_buffer_1_out, controlled_buffer_1_out_2;
  wire [7:0] A_q, W_q;

  Clock #(.highDuration(1), .lowDuration(1)) clock_1 (.out(clock_1_out));
  assign {controlled_buffer_1_out_2, controlled_buffer_1_out} = AEN ? A_q : 8'bz;  // Controlled_Buffer controlled_buffer_1
  Register #(.width(8), .trigger("rising"), .Select("low")) A (
    .D(\公用输入端 ), .en(AEN), .Q(A_q), .clk(clock_1_out), .clr(Reset));
  Hex_Digit_Display hex_digit_display_1 (.value(controlled_buffer_1_out_2));  // open: dp
  Hex_Digit_Display hex_digit_display_2 (.value(controlled_buffer_1_out));  // open: dp
  Register #(.width(8), .trigger("rising"), .Select("low")) W (
    .D(\公用输入端 ), .en(WEN), .Q(W_q), .clk(clock_1_out), .clr(Reset));
  assign {controlled_buffer_1_out_2, controlled_buffer_1_out} = WEN ? W_q : 8'bz;  // Controlled_Buffer controlled_buffer_2

  // Notes on the sheet:
  //   可控三态门
endmodule
