// Logisim project 2018214184-李嘉文-实验二 运算器实验.circ as structural Verilog: 6 circuits, main circuit main
module main (
  input  [7:0] A,
  input  Cy,
  input  [2:0] OP,
  input  [1:0] Ad
);

  wire [3:0] \多功能运算器_1_out_7 , \多功能运算器_1_out_7_2 ;
  wire [7:0] R0_q, R1_q, R2_q, R3_q, WData;

  Hex_Digit_Display hex_digit_display_1 (.value(\多功能运算器_1_out_7_2 ));  // open: dp
  \多功能运算器  \u_多功能运算器_1  (
    .S2(OP[2]), .S1(OP[1]), .S0(OP[0]), .Cy(Cy), .in_5(A), .in_6(WData),
    .out_7({\多功能运算器_1_out_7_2 , \多功能运算器_1_out_7 }));
  Hex_Digit_Display hex_digit_display_2 (.value(\多功能运算器_1_out_7 ));  // open: dp
  Register #(.width(8), .trigger("rising"), .Select("low")) R0 (.Q(R0_q));  // open: D, en, clk, clr
  Register #(.width(8), .trigger("rising"), .Select("low")) R1 (.Q(R1_q));  // open: D, en, clk, clr
  Register #(.width(8), .trigger("rising"), .Select("low")) R2 (.Q(R2_q));  // open: D, en, clk, clr
  Register #(.width(8), .trigger("rising"), .Select("low")) R3 (.Q(R3_q));  // open: D, en, clk, clr
  Multiplexer #(.select(2), .width(8), .disabled("Z"), .enable("false")) multiplexer_1 (
    .in0(R0_q), .in1(R1_q), .in2(R2_q), .in3(R3_q), .out(WData), .sel(Ad));

  // Other names for the same wires on the sheet: S0 = OP[0]; S1 = OP[1]; S2 = OP[2]; Ri[1:0] = Ad
endmodule

module \多功能运算器  (
  input  S2,
  input  S1,
  input  S0,
  input  Cy,
  input  [7:0] in_5,
  input  [7:0] in_6,
  output [7:0] out_7
);

  wire and_1_out, and_2_out, controlled_buffer_1_out, controlled_buffer_2_out;
  wire [7:0] L0, L1, L2, L3, L4, L5;

  and and_1 (and_1_out, S2, ~S1, ~S0);  // AND_Gate
  and and_2 (and_2_out, S2, ~S1, S0);  // AND_Gate
  assign controlled_buffer_1_out = and_1_out ? Cy : 1'bz;  // Controlled_Buffer controlled_buffer_1
  Adder #(.width(8)) adder_1 (.a(in_5), .b(in_6), .out(L0), .cin(controlled_buffer_1_out));  // open: cout
  assign controlled_buffer_2_out = and_2_out ? Cy : 1'bz;  // Controlled_Buffer controlled_buffer_2
  Subtractor #(.width(8)) subtractor_1 (.a(in_5), .b(in_6), .out(L1), .bin(controlled_buffer_2_out));  // open: bout
  \或运算  \u_或运算_1  (.in_1(in_5), .in_2(in_6), .out_3(L2));
  \与运算  \u_与运算_1  (.in_1(in_5), .out_3(L3), .in_2(in_6));
  \取反  \u_取反_1  (.out_2(L4), .in_1(in_5));
  \传输  \u_传输_1  (.in_1(in_5), .out_2(L5));
  Multiplexer #(.select(3), .width(8), .disabled(0), .enable("false")) multiplexer_1 (
    .in0(L0), .in1(L1), .in2(L2), .in3(L3), .in4(L0), .in5(L1), .in6(L4), .in7(L5), .out(out_7),
    .sel({S2, S1, S0}));
endmodule

module \或运算  (
  input  [7:0] in_1,
  input  [7:0] in_2,
  output [7:0] out_3
);

  assign out_3 = in_1 | in_2;  // OR_Gate or_1, 8 bits wide
endmodule

module \与运算  (
  input  [7:0] in_1,
  input  [7:0] in_2,
  output [7:0] out_3
);

  assign out_3 = in_1 & in_2;  // AND_Gate and_1, 8 bits wide
endmodule

module \取反  (
  input  [7:0] in_1,
  output [7:0] out_2
);

  assign out_2 = ~in_1;  // NOT_Gate not_1, 8 bits wide
endmodule

module \传输  (
  input  [7:0] in_1,
  output [7:0] out_2
);


  assign out_2 = in_1;
endmodule
