// Logisim project 2018214184-李嘉文-实验四 模型机综合实验（模拟数据通路）.circ as structural Verilog: 7 circuits, main circuit main
module main (
  input  [7:0] \地址输入 ,
  input  in_2
);

  wire CLK, controlled_buffer_4_out, controlled_buffer_5_out, controlled_buffer_7_out, T0, T1, T2;
  wire [7:0] ACC_q, controlled_buffer_1_out, controlled_buffer_2_out, controlled_buffer_3_out,
       controlled_buffer_6_out, MAR_q, R1_q, ram_1_data;

  Clock #(.highDuration(1), .lowDuration(1)) clock_1 (.out(CLK));
  LED #(.active("true")) led_1 (.in(T0));
  LED #(.active("true")) led_2 (.in(T1));
  assign controlled_buffer_1_out = T0 ? \地址输入  : 8'bz;  // Controlled_Buffer controlled_buffer_1
  LED #(.active("true")) led_3 (.in(T2));
  Time_03 time_03_1 (.Clock(CLK), .RSet(in_2), .T0(T0), .T1(T1), .T2(T2));
  assign controlled_buffer_2_out = T0 ? controlled_buffer_1_out : 8'bz;  // Controlled_Buffer controlled_buffer_2
  assign controlled_buffer_3_out = T1 ? controlled_buffer_1_out : 8'bz;  // Controlled_Buffer controlled_buffer_3
  Register #(.width(8), .trigger("falling"), .Select("low")) MAR (
    .D(controlled_buffer_2_out), .Q(MAR_q), .clk(controlled_buffer_4_out), .clr(in_2));  // open: en
  assign controlled_buffer_4_out = T0 ? CLK : 1'bz;  // Controlled_Buffer controlled_buffer_4
  Register #(.width(8), .trigger("falling"), .Select("low")) ACC (
    .D(controlled_buffer_3_out), .Q(ACC_q), .clk(controlled_buffer_5_out), .clr(in_2));  // open: en
  assign controlled_buffer_5_out = T1 ? CLK : 1'bz;  // Controlled_Buffer controlled_buffer_5
  Hex_Digit_Display hex_digit_display_1 (.value(ACC_q[7:4]));  // open: dp
  Hex_Digit_Display hex_digit_display_2 (.value(ACC_q[3:0]));  // open: dp
  assign controlled_buffer_6_out = T2 ? ACC_q : 8'bz;  // Controlled_Buffer controlled_buffer_6
  RAM #(.addrWidth(8), .dataWidth(8), .bus("combined"), .Select("high")) ram_1 (
    .addr(MAR_q), .data(ram_1_data));  // open: sel, clk, ld, clr
  Register #(.width(8), .trigger("falling"), .Select("low")) R1 (
    .D(controlled_buffer_6_out), .Q(R1_q), .clk(controlled_buffer_7_out), .clr(in_2));  // open: en
  assign controlled_buffer_7_out = T2 ? CLK : 1'bz;  // Controlled_Buffer controlled_buffer_7
  assign controlled_buffer_1_out = T1 ? ram_1_data : 8'bz;  // Controlled_Buffer controlled_buffer_8
  Hex_Digit_Display hex_digit_display_3 (.value(R1_q[7:4]));  // open: dp
  Hex_Digit_Display hex_digit_display_4 (.value(R1_q[3:0]));  // open: dp

  // Other names for the same wires on the sheet: RST = in_2

  // Notes on the sheet:
  //   要求：自己设计一个复杂的电路
  //   1、第一拍给地址、第二拍读出的数据送入寄存器、第三拍寄存器数据送入R0
endmodule

module \指令01  (
  input  [7:0] in_1,
  input  in_2
);

  wire CLK, controlled_buffer_3_out, T0, time_02_1_t1;
  wire [7:0] ACC_q, controlled_buffer_1_out, controlled_buffer_2_out;

  Clock #(.highDuration(1), .lowDuration(1)) clock_1 (.out(CLK));
  LED #(.active("true")) led_1 (.in(T0));
  Time_02 time_02_1 (.Clock(CLK), .RSet(in_2), .T0(T0), .T1(time_02_1_t1));
  assign controlled_buffer_1_out = T0 ? in_1 : 8'bz;  // Controlled_Buffer controlled_buffer_1
  LED #(.active("true")) led_2 (.in(time_02_1_t1));
  assign controlled_buffer_2_out = T0 ? controlled_buffer_1_out : 8'bz;  // Controlled_Buffer controlled_buffer_2
  Register #(.width(8), .trigger("falling"), .Select("low")) ACC (
    .D(controlled_buffer_2_out), .Q(ACC_q), .clk(controlled_buffer_3_out), .clr(in_2));  // open: en
  assign controlled_buffer_3_out = T0 ? CLK : 1'bz;  // Controlled_Buffer controlled_buffer_3
  Hex_Digit_Display hex_digit_display_1 (.value(ACC_q[7:4]));  // open: dp
  Hex_Digit_Display hex_digit_display_2 (.value(ACC_q[3:0]));  // open: dp

  // Other names for the same wires on the sheet: RST = in_2

  // Notes on the sheet:
  //   向寄存器里送数据
  //   1、可控缓冲门
  //   2、寄存器写入脉冲（下沿）
endmodule

module \指令02  (
  input  [7:0] in_1,
  input  in_2
);

  wire CLK, controlled_buffer_3_out, or_1_out, or_2_out, T0, T1;
  wire [7:0] ACC_q, controlled_buffer_1_out, controlled_buffer_2_out, R0_q;

  Clock #(.highDuration(1), .lowDuration(1)) clock_1 (.out(CLK));
  LED #(.active("true")) led_1 (.in(T0));
  Time_02 time_02_1 (.Clock(CLK), .RSet(in_2), .T0(T0), .T1(T1));
  assign controlled_buffer_1_out = T0 ? in_1 : 8'bz;  // Controlled_Buffer controlled_buffer_1
  LED #(.active("true")) led_2 (.in(T1));
  assign controlled_buffer_2_out = or_1_out ? controlled_buffer_1_out : 8'bz;  // Controlled_Buffer controlled_buffer_2
  or or_1 (or_1_out, T0, T1);
  Register #(.width(8), .trigger("falling"), .Select("low")) ACC (
    .D(controlled_buffer_2_out), .Q(ACC_q), .clk(controlled_buffer_3_out), .clr(in_2));  // open: en
  assign controlled_buffer_3_out = or_2_out ? CLK : 1'bz;  // Controlled_Buffer controlled_buffer_3
  or or_2 (or_2_out, T0, T1);
  assign controlled_buffer_1_out = T1 ? R0_q : 8'bz;  // Controlled_Buffer controlled_buffer_4
  Register #(.width(8), .trigger("falling"), .Select("low")) R0 (.Q(R0_q), .clr(in_2));  // open: D, en, clk
  Hex_Digit_Display hex_digit_display_1 (.value(ACC_q[7:4]));  // open: dp
  Hex_Digit_Display hex_digit_display_2 (.value(ACC_q[3:0]));  // open: dp

  // Other names for the same wires on the sheet: RST = in_2

  // Notes on the sheet:
  //   两拍分别向寄存器里送数据
  //   2、写入脉冲（下沿）控制
  //   1、节拍控制（第一拍数据直接送入寄存器、第二拍R0的数据送入）
endmodule

module \指令03  (
  input  [7:0] in_1,
  input  in_2
);

  wire CLK, controlled_buffer_4_out, controlled_buffer_5_out, T0, T1;
  wire [7:0] ACC_q, controlled_buffer_1_out, controlled_buffer_2_out, controlled_buffer_3_out, MAR_q,
       ram_1_data;

  Clock #(.highDuration(1), .lowDuration(1)) clock_1 (.out(CLK));
  LED #(.active("true")) led_1 (.in(T0));
  assign controlled_buffer_1_out = T0 ? in_1 : 8'bz;  // Controlled_Buffer controlled_buffer_1
  Time_02 time_02_1 (.Clock(CLK), .RSet(in_2), .T0(T0), .T1(T1));
  LED #(.active("true")) led_2 (.in(T1));
  assign controlled_buffer_2_out = T0 ? controlled_buffer_1_out : 8'bz;  // Controlled_Buffer controlled_buffer_2
  assign controlled_buffer_3_out = T1 ? controlled_buffer_1_out : 8'bz;  // Controlled_Buffer controlled_buffer_3
  Register #(.width(8), .trigger("falling"), .Select("low")) MAR (
    .D(controlled_buffer_2_out), .Q(MAR_q), .clk(controlled_buffer_4_out), .clr(in_2));  // open: en
  assign controlled_buffer_4_out = T0 ? CLK : 1'bz;  // Controlled_Buffer controlled_buffer_4
  Register #(.width(8), .trigger("falling"), .Select("low")) ACC (
    .D(controlled_buffer_3_out), .Q(ACC_q), .clk(controlled_buffer_5_out), .clr(in_2));  // open: en
  assign controlled_buffer_5_out = T1 ? CLK : 1'bz;  // Controlled_Buffer controlled_buffer_5
  Hex_Digit_Display hex_digit_display_1 (.value(ACC_q[7:4]));  // open: dp
  Hex_Digit_Display hex_digit_display_2 (.value(ACC_q[3:0]));  // open: dp
  RAM #(.addrWidth(8), .dataWidth(8), .bus("combined"), .Select("high")) ram_1 (
    .addr(MAR_q), .data(ram_1_data));  // open: sel, clk, ld, clr
  assign controlled_buffer_1_out = T1 ? ram_1_data : 8'bz;  // Controlled_Buffer controlled_buffer_6

  // Other names for the same wires on the sheet: RST = in_2

  // Notes on the sheet:
  //   两拍分别向寄存器里送数据
  //   2、写入脉冲（下沿）控制
  //   1、节拍控制（第一拍给地址、第二拍存储器读出的数据送入寄存器）
endmodule

module Time_04 (
  input  Clock,
  input  RSet,
  output T0,
  output T1,
  output T2,
  output T3
);

  D_Flip_Flop #(.trigger("rising"), .Pre_Clr_Positions("LEGACY"), .NegatePresetClear("false"), .enable("true"), .NewFFLayout("false")) d_ff_1 (
    .clk(Clock), .D(T3), .Q(T0), .preset(RSet));  // open: Qn, en, reset
  D_Flip_Flop #(.trigger("rising"), .Pre_Clr_Positions("LEGACY"), .NegatePresetClear("false"), .enable("true"), .NewFFLayout("false")) d_ff_2 (
    .clk(Clock), .D(T0), .Q(T1), .reset(RSet));  // open: Qn, preset, en
  D_Flip_Flop #(.trigger("rising"), .Pre_Clr_Positions("LEGACY"), .NegatePresetClear("false"), .enable("true"), .NewFFLayout("false")) d_ff_3 (
    .clk(Clock), .D(T1), .Q(T2), .reset(RSet));  // open: Qn, preset, en
  D_Flip_Flop #(.trigger("rising"), .Pre_Clr_Positions("LEGACY"), .NegatePresetClear("false"), .enable("true"), .NewFFLayout("false")) d_ff_4 (
    .clk(Clock), .D(T2), .Q(T3), .reset(RSet));  // open: Qn, preset, en
endmodule

module Time_03 (
  input  Clock,
  input  RSet,
  output T0,
  output T1,
  output T2
);

  D_Flip_Flop #(.trigger("rising"), .Pre_Clr_Positions("LEGACY"), .NegatePresetClear("false"), .enable("true"), .NewFFLayout("false")) d_ff_1 (
    .clk(Clock), .D(T2), .Q(T0), .preset(RSet));  // open: Qn, en, reset
  D_Flip_Flop #(.trigger("rising"), .Pre_Clr_Positions("LEGACY"), .NegatePresetClear("false"), .enable("true"), .NewFFLayout("false")) d_ff_2 (
    .clk(Clock), .D(T0), .Q(T1), .reset(RSet));  // open: Qn, preset, en
  D_Flip_Flop #(.trigger("rising"), .Pre_Clr_Positions("LEGACY"), .NegatePresetClear("false"), .enable("true"), .NewFFLayout("false")) d_ff_3 (
    .clk(Clock), .D(T1), .Q(T2), .reset(RSet));  // open: Qn, preset, en

  // Notes on the sheet:
  //   CLK
  //   T0
  //   T1
  //   T2
  //   时序关系示意图
endmodule

module Time_02 (
  input  Clock,
  input  RSet,
  output T0,
  output T1
);

  D_Flip_Flop #(.trigger("rising"), .Pre_Clr_Positions("LEGACY"), .NegatePresetClear("false"), .enable("true"), .NewFFLayout("false")) d_ff_1 (
    .clk(Clock), .D(T1), .Q(T0), .preset(RSet));  // open: Qn, en, reset
  D_Flip_Flop #(.trigger("rising"), .Pre_Clr_Positions("LEGACY"), .NegatePresetClear("false"), .enable("true"), .NewFFLayout("false")) d_ff_2 (
    .clk(Clock), .D(T0), .Q(T1), .reset(RSet));  // open: Qn, preset, en
endmodule
