// Logisim project 二、三节拍分支.circ as structural Verilog: 1 circuit, main circuit 二、三节拍分支
module \二_三节拍分支  (
  input  Clock,
  input  RSet,
  input  \标志位 ,
  output T0,
  output T1,
  output T2
);

  wire demultiplexer_1_out0, demultiplexer_1_out1, multiplexer_1_out;

  D_Flip_Flop #(.trigger("rising"), .Pre_Clr_Positions("LEGACY"), .NegatePresetClear("false"), .enable("true"), .NewFFLayout("false")) d_ff_1 (
    .clk(Clock), .D(T2), .Q(T0), .preset(RSet));  // open: Qn, en, reset
  Demultiplexer #(.select(1), .width(1), .tristate("false"), .disabled("Z"), .enable("false")) demultiplexer_1 (
    .out0(demultiplexer_1_out0), .out1(demultiplexer_1_out1), .in(T0), .sel(\标志位 ));
  D_Flip_Flop #(.trigger("rising"), .Pre_Clr_Positions("LEGACY"), .NegatePresetClear("false"), .enable("true"), .NewFFLayout("false")) d_ff_2 (
    .clk(Clock), .D(demultiplexer_1_out0), .Q(T1), .reset(RSet));  // open: Qn, preset, en
  Multiplexer #(.select(1), .width(1), .disabled("Z"), .enable("false")) multiplexer_1 (
    .in0(T1), .in1(demultiplexer_1_out1), .out(multiplexer_1_out), .sel(\标志位 ));
  D_Flip_Flop #(.trigger("rising"), .Pre_Clr_Positions("LEGACY"), .NegatePresetClear("false"), .enable("true"), .NewFFLayout("false")) d_ff_3 (
    .clk(Clock), .D(multiplexer_1_out), .Q(T2), .reset(RSet));  // open: Qn, preset, en
endmodule
